# Fritzing sketch Dog_Buttons_ Fritzing_Schematic (saved by Fritzing 0.9.3b)
breadboards: 2

parts:
  Part1 = Adafruit MAX98357A I2S 3W Class D Amplifier [part_number="Adafruit #3006"]
  BAT1 = 18650 battery holder [package=battery-18650-kit]
  A2 = j5019
  A3 = ESP32-S3-WROOM-1-N16R8 dev board
  A4 = Micro SD card reader
  S3 = Pushbutton [package="[THT]"]
  R1 = Resistor [tolerance=±5% resistance=100k package=THT]
  C1 = Electrolytic Capacitor [capacitance=100µF voltage=16V package="100 mil [THT, electrolytic]"]
  C2 = Ceramic Capacitor [capacitance=0.1µF voltage=16V package="100 mil [THT, multilayer]"]
  SP1 = SPEAKER [package=pcb_mount_speaker]
  S4 = Pushbutton [package="[THT]"]
  LED1 = LED - 5mm [color="Blue (470nm)" package="5 mm [THT]"]
  LED2 = LED - 5mm [color="White (6500K)" package="5 mm [THT]"]
  R2 = Resistor [tolerance=±5% resistance=220 package=THT]
  R3 = Resistor [tolerance=±5% resistance=220 package=THT]

nets:
  N1: Part1.VIN, A2.Pin_1, A3.Pin_21, C1.+, C2.0
  N2: Part1.GND, BAT1.+, A2.Pin_2, A2.Pin_4, A2.Pin_5, A3.Pin_22, A3.Pin_23, A3.Pin_24, A3.Pin_44, A4.Pin_6, S3.Pin_1, S3.Pin_2, R1.Pin_0, C1.-, C2.1, S4.Pin_1, S4.Pin_2, R2.Pin_1, R3.Pin_0
  N3: Part1.GAIN, R1.Pin_1
  N4: Part1.DIN, A3.Pin_28
  N5: Part1.BCLK, A3.Pin_27
  N6: Part1.LRCLK, A3.Pin_29
  N7: Part1.VO-, SP1.+
  N8: Part1.VO+, SP1.-
  N9: BAT1.-, A2.Pin_6
  N10: A3.Pin_1, A3.Pin_2, A4.Pin_1
  N11: A3.Pin_4, S3.Pin_3, S3.Pin_4
  N12: A3.Pin_5, LED1.anode
  N13: A3.Pin_9, A4.Pin_3
  N14: A3.Pin_10, A4.Pin_4
  N15: A3.Pin_11, A4.Pin_5
  N16: A3.Pin_12, S4.Pin_3, S4.Pin_4
  N17: A3.Pin_14, LED2.anode
  N18: A3.Pin_16, A4.Pin_2
  N19: LED1.cathode, R2.Pin_0
  N20: LED2.cathode, R3.Pin_1

custom parts:
  Adafruit MAX98357A I2S 3W Class D Amplifier: Listen to this good news - we now have an all in one digital audio amp breakout board that works incredibly well with the Raspberry Pi! If you're looking for an easy and low cost way to get you digital sound files bumpin' then the MAX08357 I2S Amp Breakout is for you. It takes standard I2S digital audio input and, not only decodes it into analog, but also amplifies it directly into a speaker.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
  18650 battery holder: 18650 Battery Holder identical to the dual battery version.
  j5019: This module is a small single cell lithium battery charging module which also includes a 1A step-up (boost) converter for powering a large range of applications.
  ESP32-S3-WROOM-1-N16R8 dev board: ESP32-S3 WIFI+BLE5.0 Development Board ESP32-S3-WROOM-1-N16R8(16M Flash/8SRAM).
  Micro SD card reader: Micro SD card reader.
